# Fritzing sketch wiring (saved by Fritzing 0.9.4)
circuit board: 8.46667cm x 5.64444cm

parts:
  A1 = Raspberry Pi 5
  S1 = H-Bridge with L298N
  M4 = DC Motor
  M2 = DC Motor
  M5 = DC Motor
  M6 = DC Motor
  JACK2 = 2.1mm_Barrel_Jack_with_Terminal_Block
  J2 = arducam [form="♀ (female)"]  # not connected

nets:
  GND: A1.GND, A1.Fan-GND, S1.GND, JACK2.connector2
  N1: A1.GPIO18, S1.IN1
  N2: A1.GPIO12, S1.ENA
  N3: A1.GPIO13, S1.ENB
  N4: A1.GPIO19, S1.IN2
  N5: A1.GPIO20, S1.IN3
  N6: A1.GPIO21, S1.IN4
  N7: S1.12V, JACK2.connector1
  N8: S1.M1-01, M2.pin_2, M5.pin_2
  N9: S1.M1-02, M2.pin_1, M5.pin_1
  N10: S1.M2-01, M4.pin_2, M6.pin_2
  N11: S1.M2-02, M4.pin_1, M6.pin_1

custom parts:
  Raspberry Pi 5: The RPi5, a faster version of the awesome Raspberry Pi4B ARM Board with 40 pin gpio.
  H-Bridge with L298N: h-bridge
