# Fritzing sketch wiring_bts7960 (saved by Fritzing 0.9.4)

parts:
  A1 = drv-1012
  A2 = Raspberry Pi 5

nets:
  N1: A1.Pin_1, A2.GND
  N2: A1.Pin_3, A2.GPIO24
  N3: A1.Pin_4, A2.GPIO19
  N4: A1.Pin_5, A2.5V, A2.Fan-5V
  N5: A1.Pin_7, A2.GPIO23
  N6: A1.Pin_8, A2.GPIO18

custom parts:
  drv-1012: .The BTS7960 is a fully integrated high current H bridge module for motor drive applications.
  Raspberry Pi 5: The RPi5, a faster version of the awesome Raspberry Pi4B ARM Board with 40 pin gpio.
